// Logisim project electronics project.circ as structural Verilog: 1 circuit, main circuit main
module main (
);

  wire button_1_out, button_2_out, button_3_out, button_4_out, d_ff_1_qn, d_ff_2_qn, d_ff_3_qn, d_ff_4_qn,
       d_ff_5_q, d_ff_5_qn, d_ff_6_q, d_ff_6_qn, d_ff_7_q, d_ff_7_qn, d_ff_8_q, d_ff_8_qn, nand_1_out,
       nand_2_out, nand_3_out, nand_4_out, nand_5_out, nand_6_out, nand_7_out, nand_8_out, nand_9_out,
       nand_10_out, nand_11_out, nand_12_out, nand_13_out, nand_14_out, nand_15_out, nand_16_out,
       nand_17_out, nand_18_out;

  LED led_1 (.in(d_ff_7_q));
  LED led_2 (.in(d_ff_5_q));
  LED led_3 (.in(d_ff_8_q));
  Button button_1 (.out(button_1_out));
  Button button_2 (.out(button_2_out));
  LED led_4 (.in(d_ff_6_q));
  Button button_3 (.out(button_3_out));
  Button button_4 (.out(button_4_out));
  D_Flip_Flop d_ff_1 (.clk(button_1_out), .D(d_ff_5_qn), .Qn(d_ff_1_qn));  // open: Q, preset, en, reset
  D_Flip_Flop d_ff_2 (.clk(button_2_out), .D(d_ff_6_qn), .Qn(d_ff_2_qn));  // open: Q, preset, en, reset
  D_Flip_Flop d_ff_3 (.clk(button_3_out), .D(d_ff_7_qn), .Qn(d_ff_3_qn));  // open: Q, preset, en, reset
  D_Flip_Flop d_ff_4 (.clk(button_4_out), .D(d_ff_8_qn), .Qn(d_ff_4_qn));  // open: Q, preset, en, reset
  D_Flip_Flop d_ff_5 (.clk(button_1_out), .D(d_ff_1_qn), .Q(d_ff_5_q), .Qn(d_ff_5_qn));  // open: preset, en, reset
  D_Flip_Flop d_ff_6 (.clk(button_2_out), .D(d_ff_2_qn), .Q(d_ff_6_q), .Qn(d_ff_6_qn));  // open: preset, en, reset
  D_Flip_Flop d_ff_7 (.clk(button_3_out), .D(d_ff_3_qn), .Q(d_ff_7_q), .Qn(d_ff_7_qn));  // open: preset, en, reset
  D_Flip_Flop d_ff_8 (.clk(button_4_out), .D(d_ff_4_qn), .Q(d_ff_8_q), .Qn(d_ff_8_qn));  // open: preset, en, reset
  nand nand_1 (nand_1_out, d_ff_5_q, d_ff_5_q, d_ff_6_q, d_ff_6_q);
  nand nand_2 (nand_2_out, d_ff_7_q, d_ff_7_q, d_ff_8_q, d_ff_8_q);
  nand nand_3 (nand_3_out, d_ff_5_q, d_ff_5_q, nand_1_out);
  nand nand_4 (nand_4_out, nand_1_out, d_ff_6_q, d_ff_6_q);
  nand nand_5 (nand_5_out, d_ff_7_q, d_ff_7_q, nand_2_out);
  nand nand_6 (nand_6_out, nand_2_out, d_ff_8_q, d_ff_8_q);
  nand nand_7 (nand_7_out, nand_3_out, nand_3_out, nand_4_out, nand_4_out);
  nand nand_8 (nand_8_out, nand_5_out, nand_5_out, nand_6_out, nand_6_out);
  nand nand_9 (nand_9_out, nand_7_out, nand_7_out, 1'b0);
  nand nand_10 (nand_10_out, nand_8_out, nand_8_out, nand_13_out);
  nand nand_11 (nand_11_out, nand_7_out, nand_7_out, nand_9_out, nand_9_out);
  nand nand_12 (nand_12_out, nand_9_out, 1'b0);
  nand nand_13 (nand_13_out, nand_9_out, nand_1_out);
  nand nand_14 (nand_14_out, nand_8_out, nand_8_out, nand_10_out, nand_10_out);
  nand nand_15 (nand_15_out, nand_10_out, nand_13_out);
  nand nand_16 (nand_16_out, nand_11_out, nand_11_out, nand_12_out, nand_12_out);
  nand nand_17 (nand_17_out, nand_14_out, nand_14_out, nand_15_out, nand_15_out);
  nand nand_18 (nand_18_out, nand_10_out, nand_2_out);
  LED led_5 (.in(nand_17_out));
  LED led_6 (.in(nand_16_out));
  LED led_7 (.in(nand_18_out));

  // Notes on the sheet:
  //   +
  //   A0
  //   B0
  //   A1
  //   B1
  //   Out - 1
  //   Out - 2
  //   Carry - out
  //   =
  //   Carry
endmodule
